# Fritzing sketch simon (saved by Fritzing 0.9.3b)
breadboards: 1

parts:
  Part1 = Arduino Uno (Rev3)
  S1 = Pushbutton [package="[THT]"]
  S2 = Pushbutton [package="[THT]"]
  S3 = Pushbutton [package="[THT]"]
  S4 = Pushbutton [package="[THT]"]
  J1 = Piezo Speaker
  LED1 = LED - 5mm [color="Red (633nm)" package="5 mm [THT]"]
  LED2 = LED - 5mm [color="Green (565nm)" package="5 mm [THT]"]
  LED3 = LED - 5mm [color="Blue (505nm)" package="5 mm [THT]"]
  LED4 = LED - 5mm [color="Yellow (595nm)" package="5 mm [THT]"]
  R1 = Resistor [tolerance=±5% resistance=330 package=THT]
  R2 = Resistor [tolerance=±5% resistance=330 package=THT]
  R3 = Resistor [tolerance=±5% resistance=330 package=THT]
  R4 = Resistor [tolerance=±5% resistance=330 package=THT]

nets:
  N1: Part1.D8, R3.Pin_0
  N2: Part1.D9_PWM, R4.Pin_0
  N3: Part1.D10_PWM/SS, J1.pin2
  N4: Part1.D11_PWM/MOSI, J1.pin1
  N5: Part1.D2, S1.Pin_3, S1.Pin_4
  N6: Part1.D3_PWM, R2.Pin_0
  N7: Part1.D4, R1.Pin_0
  N8: Part1.D5_PWM, S2.Pin_3, S2.Pin_4
  N9: Part1.D6_PWM, S3.Pin_3, S3.Pin_4
  N10: Part1.D7, S4.Pin_3, S4.Pin_4
  N11: Part1.GND, S1.Pin_1, S1.Pin_2, S2.Pin_1, S2.Pin_2, S3.Pin_1, S3.Pin_2, S4.Pin_1, S4.Pin_2, LED1.cathode, LED2.cathode, LED3.cathode, LED4.cathode
  N12: LED1.anode, R4.Pin_1
  N13: LED2.anode, R3.Pin_1
  N14: LED3.anode, R2.Pin_1
  N15: LED4.anode, R1.Pin_1
