# Fritzing sketch simon_3 (saved by Fritzing 0.9.3b)
breadboards: 1

parts:
  Part1 = Arduino Uno (Rev3)
  S1 = Pushbutton [package="[THT]"]
  S2 = Pushbutton [package="[THT]"]
  S3 = Pushbutton [package="[THT]"]
  J1 = Piezo Speaker
  LED1 = LED - 5mm [color="Green (565nm)" package="5 mm [THT]"]
  LED2 = LED - 5mm [color="Red (635nm)" package="5 mm [THT]"]
  LED3 = LED - 5mm [color="Yellow (595nm)" package="5 mm [THT]"]
  R1 = Resistor [tolerance=±5% resistance=330 package=THT]
  R2 = Resistor [tolerance=±5% resistance=330 package=THT]
  R3 = Resistor [tolerance=±5% resistance=330 package=THT]

nets:
  N1: Part1.D8, S3.Pin_1, S3.Pin_2
  N2: Part1.D9_PWM, S2.Pin_1, S2.Pin_2
  N3: Part1.D10_PWM/SS, S1.Pin_1, S1.Pin_2
  N4: Part1.D2, R1.Pin_0
  N5: Part1.D3_PWM, R2.Pin_0
  N6: Part1.D4, R3.Pin_0
  N7: Part1.D7, J1.pin2
  N8: Part1.GND, S1.Pin_3, S1.Pin_4, S2.Pin_3, S2.Pin_4, S3.Pin_3, S3.Pin_4, J1.pin1, LED1.cathode, LED2.cathode, LED3.cathode
  N9: LED1.anode, R1.Pin_1
  N10: LED2.anode, R2.Pin_1
  N11: LED3.anode, R3.Pin_1
